// Logisim project APS DEF.circ as structural Verilog
module \Relógio_digital  (
);

  wire and_1_out, CLK_0_5_2_sa, CLK_0_5_2_sb, CLK_0_5_2_sc, CLK_0_5_2_sd, CLK_0_5_2_vai1, CLK_0_5_sa,
       CLK_0_5_sb, CLK_0_5_sc, CLK_0_5_sd, CLK_0_5_vai1, CLK_0_9_2_sa, CLK_0_9_2_sb, CLK_0_9_2_sc,
       CLK_0_9_2_sd, CLK_0_9_2_vai1, CLK_0_9_sa, CLK_0_9_sb, CLK_0_9_sc, CLK_0_9_sd, CLK_0_9_vai1,
       CLK_0__2_sa, CLK_0__2_sb, CLK_0__2_sc, CLK_0__2_sd, CLK_I_sa, CLK_I_sb, CLK_I_sc, CLK_I_sd,
       CLK_I_vai1, clock_1_out, DECOD_2_a_2, DECOD_2_b_2, DECOD_2_c_2, DECOD_2_d_2, DECOD_2_e, DECOD_2_f,
       DECOD_2_g, DECOD_3_a_2, DECOD_3_b_2, DECOD_3_c_2, DECOD_3_d_2, DECOD_3_e, DECOD_3_f, DECOD_3_g,
       DECOD_4_a_2, DECOD_4_b_2, DECOD_4_c_2, DECOD_4_d_2, DECOD_4_e, DECOD_4_f, DECOD_4_g, DECOD_5_a_2,
       DECOD_5_b_2, DECOD_5_c_2, DECOD_5_d_2, DECOD_5_e, DECOD_5_f, DECOD_5_g, DECOD_6_a_2, DECOD_6_b_2,
       DECOD_6_c_2, DECOD_6_d_2, DECOD_6_e, DECOD_6_f, DECOD_6_g, DECOD_a_2, DECOD_b_2, DECOD_c_2, DECOD_d_2,
       DECOD_e, DECOD_f, DECOD_g, multiplexer_1_out, or_1_out, RESET_out, st_cls_1_s;

  Button RESET (.out(RESET_out));
  Multiplexer #(.enable("false")) multiplexer_1 (
    .in0(or_1_out), .in1(and_1_out), .out(multiplexer_1_out), .sel(and_1_out));
  or or_1 (or_1_out, RESET_out, st_cls_1_s);
  and and_1 (and_1_out, ~DECOD_a_2, DECOD_b_2, DECOD_c_2, ~DECOD_d_2, ~DECOD_e, ~DECOD_f, ~DECOD_g, DECOD_2_a_2, DECOD_2_b_2, ~DECOD_2_c_2, DECOD_2_d_2, DECOD_2_e, ~DECOD_2_f, DECOD_2_g);  // AND_Gate
  clock_de_hora CLK_0__2 (
    .CLOCK(CLK_0_9_vai1), .RESET(multiplexer_1_out), .sA(CLK_0__2_sa), .sB(CLK_0__2_sb), .sC(CLK_0__2_sc),
    .sD(CLK_0__2_sd));  // open: vai1
  BCD_8421_P_7 DECOD (
    .D(CLK_0__2_sd), .C(CLK_0__2_sc), .B(CLK_0__2_sb), .A(CLK_0__2_sa), .a_2(DECOD_a_2), .b_2(DECOD_b_2),
    .c_2(DECOD_c_2), .d_2(DECOD_d_2), .e(DECOD_e), .f(DECOD_f), .g(DECOD_g));
  _7_Segment_Display u_7_segment_display_1 (
    .g(DECOD_g), .f(DECOD_f), .a(DECOD_a_2), .b(DECOD_b_2), .e(DECOD_e), .d(DECOD_d_2), .c(DECOD_c_2));  // open: dp
  clock_0_a_9 CLK_0_9 (
    .CLOCK(CLK_0_5_vai1), .RESET(multiplexer_1_out), .sA(CLK_0_9_sa), .sB(CLK_0_9_sb), .sC(CLK_0_9_sc),
    .sD(CLK_0_9_sd), .vai1(CLK_0_9_vai1));
  _7_Segment_Display u_7_segment_display_2 (
    .g(DECOD_2_g), .f(DECOD_2_f), .a(DECOD_2_a_2), .b(DECOD_2_b_2), .e(DECOD_2_e), .d(DECOD_2_d_2),
    .c(DECOD_2_c_2));  // open: dp
  LED led_1 (.in(clock_1_out));
  LED led_2 (.in(clock_1_out));
  BCD_8421_P_7 DECOD_2 (
    .D(CLK_0_9_sd), .C(CLK_0_9_sc), .B(CLK_0_9_sb), .A(CLK_0_9_sa), .a_2(DECOD_2_a_2), .b_2(DECOD_2_b_2),
    .c_2(DECOD_2_c_2), .d_2(DECOD_2_d_2), .e(DECOD_2_e), .f(DECOD_2_f), .g(DECOD_2_g));
  LED led_3 (.in(clock_1_out));
  LED led_4 (.in(clock_1_out));
  clock_de_0_a_5 CLK_0_5 (
    .CLOCK(CLK_0_9_2_vai1), .RESET(multiplexer_1_out), .sA(CLK_0_5_sa), .sB(CLK_0_5_sb), .sC(CLK_0_5_sc),
    .sD(CLK_0_5_sd), .vai1(CLK_0_5_vai1));
  _7_Segment_Display u_7_segment_display_3 (
    .g(DECOD_3_g), .f(DECOD_3_f), .a(DECOD_3_a_2), .b(DECOD_3_b_2), .e(DECOD_3_e), .d(DECOD_3_d_2),
    .c(DECOD_3_c_2));  // open: dp
  clock_0_a_9 CLK_0_9_2 (
    .CLOCK(CLK_0_5_2_vai1), .RESET(multiplexer_1_out), .sA(CLK_0_9_2_sa), .sB(CLK_0_9_2_sb),
    .sC(CLK_0_9_2_sc), .sD(CLK_0_9_2_sd), .vai1(CLK_0_9_2_vai1));
  BCD_8421_P_7 DECOD_3 (
    .D(CLK_0_5_sd), .C(CLK_0_5_sc), .B(CLK_0_5_sb), .A(CLK_0_5_sa), .a_2(DECOD_3_a_2), .b_2(DECOD_3_b_2),
    .c_2(DECOD_3_c_2), .d_2(DECOD_3_d_2), .e(DECOD_3_e), .f(DECOD_3_f), .g(DECOD_3_g));
  BCD_8421_P_7 DECOD_4 (
    .D(CLK_0_9_2_sd), .C(CLK_0_9_2_sc), .B(CLK_0_9_2_sb), .A(CLK_0_9_2_sa), .a_2(DECOD_4_a_2),
    .b_2(DECOD_4_b_2), .c_2(DECOD_4_c_2), .d_2(DECOD_4_d_2), .e(DECOD_4_e), .f(DECOD_4_f), .g(DECOD_4_g));
  _7_Segment_Display u_7_segment_display_4 (
    .g(DECOD_4_g), .f(DECOD_4_f), .a(DECOD_4_a_2), .b(DECOD_4_b_2), .e(DECOD_4_e), .d(DECOD_4_d_2),
    .c(DECOD_4_c_2));  // open: dp
  Clock clock_1 (.out(clock_1_out));
  clock_de_0_a_5 CLK_0_5_2 (
    .CLOCK(CLK_I_vai1), .RESET(multiplexer_1_out), .sA(CLK_0_5_2_sa), .sB(CLK_0_5_2_sb), .sC(CLK_0_5_2_sc),
    .sD(CLK_0_5_2_sd), .vai1(CLK_0_5_2_vai1));
  LED led_5 (.in(clock_1_out));
  LED led_6 (.in(clock_1_out));
  clock_inicial CLK_I (
    .CLOCK(clock_1_out), .RESET(multiplexer_1_out), .sA(CLK_I_sa), .sB(CLK_I_sb), .sC(CLK_I_sc),
    .sD(CLK_I_sd), .vai1(CLK_I_vai1));
  BCD_8421_P_7 DECOD_5 (
    .D(CLK_0_5_2_sd), .C(CLK_0_5_2_sc), .B(CLK_0_5_2_sb), .A(CLK_0_5_2_sa), .a_2(DECOD_5_a_2),
    .b_2(DECOD_5_b_2), .c_2(DECOD_5_c_2), .d_2(DECOD_5_d_2), .e(DECOD_5_e), .f(DECOD_5_f), .g(DECOD_5_g));
  _7_Segment_Display u_7_segment_display_5 (
    .g(DECOD_5_g), .f(DECOD_5_f), .a(DECOD_5_a_2), .b(DECOD_5_b_2), .e(DECOD_5_e), .d(DECOD_5_d_2),
    .c(DECOD_5_c_2));  // open: dp
  _7_Segment_Display u_7_segment_display_6 (
    .g(DECOD_6_g), .f(DECOD_6_f), .a(DECOD_6_a_2), .b(DECOD_6_b_2), .e(DECOD_6_e), .d(DECOD_6_d_2),
    .c(DECOD_6_c_2));  // open: dp
  BCD_8421_P_7 DECOD_6 (
    .D(CLK_I_sd), .C(CLK_I_sc), .B(CLK_I_sb), .A(CLK_I_sa), .a_2(DECOD_6_a_2), .b_2(DECOD_6_b_2),
    .c_2(DECOD_6_c_2), .d_2(DECOD_6_d_2), .e(DECOD_6_e), .f(DECOD_6_f), .g(DECOD_6_g));
  ST_CLS st_cls_1 (
    .a(DECOD_6_a_2), .b(DECOD_6_b_2), .c(DECOD_6_b_2), .d(DECOD_6_c_2), .e(DECOD_6_e), .f(DECOD_6_f),
    .g(DECOD_6_g), .S(st_cls_1_s));
endmodule

module clock_inicial (
  input  CLOCK,
  input  RESET,
  output sA,
  output sB,
  output sC,
  output sD,
  output vai1
);

  wire and_1_out, d_ff_1_q, d_ff_2_q, d_ff_3_q, d_ff_4_q;

  and and_1 (and_1_out, ~sA, sB, ~sC, sD);  // AND_Gate
  D_Flip_Flop d_ff_1 (.clk(CLOCK), .D(sA), .Q(d_ff_1_q), .preset(vai1));  // open: Qn, en, reset
  D_Flip_Flop d_ff_2 (.clk(d_ff_1_q), .D(sB), .Q(d_ff_2_q), .preset(vai1));  // open: Qn, en, reset
  D_Flip_Flop d_ff_3 (.clk(d_ff_2_q), .D(sC), .Q(d_ff_3_q), .preset(vai1));  // open: Qn, en, reset
  D_Flip_Flop d_ff_4 (.clk(d_ff_3_q), .D(sD), .Q(d_ff_4_q), .preset(vai1));  // open: Qn, en, reset
  Multiplexer #(.enable("false")) multiplexer_1 (.in0(and_1_out), .in1(RESET), .out(vai1), .sel(RESET));
  not not_1 (sA, d_ff_1_q);
  not not_2 (sB, d_ff_2_q);
  not not_3 (sC, d_ff_3_q);
  not not_4 (sD, d_ff_4_q);
endmodule

module clock_0_a_9 (
  input  CLOCK,
  input  RESET,
  output sA,
  output sB,
  output sC,
  output sD,
  output vai1
);

  wire and_1_out, d_ff_1_q, d_ff_2_q, d_ff_3_q, d_ff_4_q;

  and and_1 (and_1_out, ~sA, sB, ~sC, sD);  // AND_Gate
  D_Flip_Flop d_ff_1 (.clk(CLOCK), .D(sA), .Q(d_ff_1_q), .preset(vai1));  // open: Qn, en, reset
  D_Flip_Flop d_ff_2 (.clk(d_ff_1_q), .D(sB), .Q(d_ff_2_q), .preset(vai1));  // open: Qn, en, reset
  D_Flip_Flop d_ff_3 (.clk(d_ff_2_q), .D(sC), .Q(d_ff_3_q), .preset(vai1));  // open: Qn, en, reset
  D_Flip_Flop d_ff_4 (.clk(d_ff_3_q), .D(sD), .Q(d_ff_4_q), .preset(vai1));  // open: Qn, en, reset
  Multiplexer #(.enable("false")) multiplexer_1 (.in0(and_1_out), .in1(RESET), .out(vai1), .sel(RESET));
  not not_1 (sA, d_ff_1_q);
  not not_2 (sB, d_ff_2_q);
  not not_3 (sC, d_ff_3_q);
  not not_4 (sD, d_ff_4_q);
endmodule

module clock_de_0_a_5 (
  input  CLOCK,
  input  RESET,
  output sA,
  output sB,
  output sC,
  output sD,
  output vai1
);

  wire and_1_out, d_ff_1_q, d_ff_2_q, d_ff_3_q, d_ff_4_q;

  and and_1 (and_1_out, ~sA, sB, sC, ~sD);  // AND_Gate
  D_Flip_Flop d_ff_1 (.clk(CLOCK), .D(sA), .Q(d_ff_1_q), .preset(vai1));  // open: Qn, en, reset
  D_Flip_Flop d_ff_2 (.clk(d_ff_1_q), .D(sB), .Q(d_ff_2_q), .preset(vai1));  // open: Qn, en, reset
  D_Flip_Flop d_ff_3 (.clk(d_ff_2_q), .D(sC), .Q(d_ff_3_q), .preset(vai1));  // open: Qn, en, reset
  D_Flip_Flop d_ff_4 (.clk(d_ff_3_q), .D(sD), .Q(d_ff_4_q), .preset(vai1));  // open: Qn, en, reset
  Multiplexer #(.enable("false")) multiplexer_1 (.in0(and_1_out), .in1(RESET), .out(vai1), .sel(RESET));
  not not_1 (sA, d_ff_1_q);
  not not_2 (sB, d_ff_2_q);
  not not_3 (sC, d_ff_3_q);
  not not_4 (sD, d_ff_4_q);
endmodule

module display (
  input  [3:0] seletor,
  output a,
  output b,
  output c,
  output d,
  output e,
  output f,
  output g
);

  Multiplexer #(.select(4), .enable("false")) multiplexer_1 (
    .in0(1'b1), .in1(1'b0), .in2(1'b1), .in3(1'b1), .in4(1'b0), .in5(1'b1), .in6(1'b1), .in7(1'b1),
    .in8(1'b1), .in9(1'b1), .out(a), .sel(seletor));  // open: in10, in11, in12, in13, in14, in15
  Multiplexer #(.select(4), .enable("false")) multiplexer_2 (
    .in0(1'b1), .in1(1'b1), .in2(1'b0), .in3(1'b1), .in4(1'b1), .in5(1'b1), .in6(1'b1), .in7(1'b1),
    .in8(1'b1), .in9(1'b1), .out(c), .sel(seletor));  // open: in10, in11, in12, in13, in14, in15
  Multiplexer #(.select(4), .enable("false")) multiplexer_3 (
    .in0(1'b1), .in1(1'b0), .in2(1'b1), .in3(1'b0), .in4(1'b0), .in5(1'b0), .in6(1'b1), .in7(1'b0),
    .in8(1'b1), .in9(1'b0), .out(e), .sel(seletor));  // open: in10, in11, in12, in13, in14, in15
  Multiplexer #(.select(4), .enable("false")) multiplexer_4 (
    .in0(1'b0), .in1(1'b0), .in2(1'b1), .in3(1'b1), .in4(1'b1), .in5(1'b1), .in6(1'b1), .in7(1'b0),
    .in8(1'b1), .in9(1'b1), .in10(1'b0), .out(g), .sel(seletor));  // open: in11, in12, in13, in14, in15
  Multiplexer #(.select(4), .enable("false")) multiplexer_5 (
    .in0(1'b1), .in1(1'b1), .in2(1'b1), .in3(1'b1), .in4(1'b1), .in5(1'b0), .in6(1'b0), .in7(1'b1),
    .in8(1'b1), .in9(1'b1), .in10(1'b0), .out(b), .sel(seletor));  // open: in11, in12, in13, in14, in15
  Multiplexer #(.select(4), .enable("false")) multiplexer_6 (
    .in0(1'b1), .in1(1'b0), .in2(1'b1), .in3(1'b1), .in4(1'b0), .in5(1'b1), .in6(1'b1), .in7(1'b0),
    .in8(1'b1), .in9(1'b1), .in10(1'b1), .out(d), .sel(seletor));  // open: in11, in12, in13, in14, in15
  Multiplexer #(.select(4), .enable("false")) multiplexer_7 (
    .in0(1'b1), .in1(1'b0), .in2(1'b0), .in3(1'b0), .in4(1'b1), .in5(1'b1), .in6(1'b1), .in7(1'b0),
    .in8(1'b1), .in9(1'b1), .in10(1'b0), .out(f), .sel(seletor));  // open: in11, in12, in13, in14, in15
endmodule

module clock_de_hora (
  input  CLOCK,
  input  RESET,
  output sA,
  output sB,
  output sC,
  output sD,
  output vai1
);

  wire and_1_out, d_ff_1_q, d_ff_2_q, d_ff_3_q, d_ff_4_q;

  and and_1 (and_1_out, ~sA, sB, ~sC, ~sD);  // AND_Gate
  D_Flip_Flop d_ff_1 (.clk(CLOCK), .D(sA), .Q(d_ff_1_q), .preset(vai1));  // open: Qn, en, reset
  D_Flip_Flop d_ff_2 (.clk(d_ff_1_q), .D(sB), .Q(d_ff_2_q), .preset(vai1));  // open: Qn, en, reset
  D_Flip_Flop d_ff_3 (.clk(d_ff_2_q), .D(sC), .Q(d_ff_3_q), .preset(vai1));  // open: Qn, en, reset
  D_Flip_Flop d_ff_4 (.clk(d_ff_3_q), .D(sD), .Q(d_ff_4_q), .preset(vai1));  // open: Qn, en, reset
  Multiplexer #(.enable("false")) multiplexer_1 (.in0(and_1_out), .in1(RESET), .out(vai1), .sel(RESET));
  not not_1 (sA, d_ff_1_q);
  not not_2 (sB, d_ff_2_q);
  not not_3 (sC, d_ff_3_q);
  not not_4 (sD, d_ff_4_q);
endmodule

module BCD_8421_P_7 (
  input  D,
  input  C,
  input  B,
  input  A,
  output a_2,
  output b_2,
  output c_2,
  output d_2,
  output e,
  output f,
  output g
);

  wire and_1_out, and_2_out, and_3_out, and_4_out, and_5_out, and_6_out, and_7_out, and_8_out, and_9_out,
       and_10_out, and_11_out, and_12_out, and_13_out, and_14_out, and_15_out, and_16_out, and_17_out,
       and_18_out, and_19_out, and_20_out, and_21_out, and_22_out, and_23_out, and_24_out, and_25_out,
       and_26_out, and_27_out, not_1_out, not_2_out, not_3_out, not_4_out, not_5_out, not_6_out, not_7_out,
       not_8_out, not_9_out, not_10_out, not_11_out, not_12_out, not_13_out, not_14_out, not_15_out,
       not_16_out, not_17_out, not_18_out, not_19_out, not_20_out, not_21_out, not_22_out, not_23_out,
       not_24_out, not_25_out, not_26_out, not_27_out, not_28_out, not_29_out, not_30_out, not_31_out,
       not_32_out, not_33_out, not_34_out, not_35_out, not_36_out, not_37_out, not_38_out, not_39_out,
       not_40_out, not_41_out, not_42_out, not_43_out, not_44_out, not_45_out, not_46_out, not_47_out,
       not_48_out, not_49_out, not_50_out, not_51_out, not_52_out;

  not not_1 (not_1_out, D);
  and and_1 (and_1_out, not_1_out, not_2_out, not_3_out);
  not not_2 (not_2_out, C);
  not not_3 (not_3_out, A);
  not not_4 (not_4_out, D);
  and and_2 (and_2_out, not_4_out, B);
  not not_5 (not_5_out, D);
  and and_3 (and_3_out, not_5_out, C, A);
  and and_4 (and_4_out, D, not_6_out, not_7_out);
  not not_6 (not_6_out, C);
  not not_7 (not_7_out, B);
  not not_8 (not_8_out, D);
  and and_5 (and_5_out, not_8_out, not_9_out);
  not not_9 (not_9_out, C);
  not not_10 (not_10_out, D);
  not not_11 (not_11_out, B);
  and and_6 (and_6_out, not_10_out, not_11_out, not_12_out);
  not not_12 (not_12_out, A);
  not not_13 (not_13_out, C);
  and and_7 (and_7_out, not_13_out, not_14_out);
  not not_14 (not_14_out, B);
  not not_15 (not_15_out, D);
  and and_8 (and_8_out, not_15_out, B, A);
  not not_16 (not_16_out, C);
  and and_9 (and_9_out, not_16_out, not_17_out);
  not not_17 (not_17_out, B);
  not not_18 (not_18_out, D);
  and and_10 (and_10_out, not_18_out, A);
  not not_19 (not_19_out, D);
  and and_11 (and_11_out, not_19_out, C);
  not not_20 (not_20_out, D);
  not not_21 (not_21_out, C);
  not not_22 (not_22_out, A);
  not not_23 (not_23_out, D);
  not not_24 (not_24_out, C);
  not not_25 (not_25_out, D);
  not not_26 (not_26_out, A);
  not not_27 (not_27_out, D);
  not not_28 (not_28_out, B);
  not not_29 (not_29_out, C);
  not not_30 (not_30_out, B);
  not not_31 (not_31_out, C);
  not not_32 (not_32_out, B);
  and and_12 (and_12_out, not_31_out, not_32_out, not_33_out);
  not not_33 (not_33_out, A);
  not not_34 (not_34_out, D);
  and and_13 (and_13_out, not_34_out, B, not_35_out);
  not not_35 (not_35_out, A);
  not not_36 (not_36_out, D);
  and and_14 (and_14_out, not_36_out, not_37_out, not_38_out);
  not not_37 (not_37_out, B);
  not not_38 (not_38_out, A);
  not not_39 (not_39_out, D);
  and and_15 (and_15_out, not_39_out, C, not_40_out);
  not not_40 (not_40_out, B);
  not not_41 (not_41_out, D);
  and and_16 (and_16_out, not_41_out, C, not_42_out);
  not not_42 (not_42_out, A);
  not not_43 (not_43_out, C);
  and and_17 (and_17_out, D, not_43_out, not_44_out);
  not not_44 (not_44_out, B);
  not not_45 (not_45_out, D);
  not not_46 (not_46_out, C);
  and and_18 (and_18_out, not_45_out, not_46_out, B);
  not not_47 (not_47_out, D);
  and and_19 (and_19_out, not_47_out, C, not_48_out);
  not not_48 (not_48_out, B);
  not not_49 (not_49_out, D);
  and and_20 (and_20_out, not_49_out, C, not_50_out);
  not not_50 (not_50_out, A);
  and and_21 (and_21_out, D, not_51_out, not_52_out);
  not not_51 (not_51_out, C);
  not not_52 (not_52_out, B);
  and and_22 (and_22_out, D, C, B, A);
  or or_1 (a_2, and_1_out, and_2_out, and_3_out, and_4_out);
  or or_2 (b_2, and_5_out, and_6_out, and_7_out, and_8_out);
  or or_3 (c_2, and_9_out, and_10_out, and_11_out);
  and and_23 (and_23_out, not_20_out, not_21_out, not_22_out);
  and and_24 (and_24_out, not_23_out, not_24_out, B);
  and and_25 (and_25_out, not_25_out, B, not_26_out);
  and and_26 (and_26_out, not_27_out, C, not_28_out, A);
  and and_27 (and_27_out, D, not_29_out, not_30_out);
  or or_4 (e, and_12_out, and_13_out);
  or or_5 (f, and_14_out, and_15_out, and_16_out, and_17_out);
  or or_6 (g, and_18_out, and_19_out, and_20_out, and_21_out, and_22_out);
  or or_7 (d_2, and_23_out, and_24_out, and_25_out, and_26_out, and_27_out);
endmodule

module ST_CLS (
  input  a,
  input  b,
  input  c,
  input  d,
  input  e,
  input  f,
  input  g,
  output S
);

  and and_1 (S, ~a, ~b, ~c, ~d, ~e, ~f, g);  // AND_Gate
endmodule
