// Logisim project APS relogio pendentre display.circ as structural Verilog: 7 circuits, main circuit CLOCK INICIAL
module CLOCK_INICIAL (
  input  CLOCK_INICIAL,
  input  PINO_RESET,
  output S___A,
  output S___B,
  output S___C,
  output S___D,
  output CX_1
);

  wire d_ff_1_q, d_ff_2_q, d_ff_3_q, d_ff_4_q, RESET_PELA_PORTA_out;

  and RESET_PELA_PORTA (RESET_PELA_PORTA_out, ~S___A, S___B, ~S___C, S___D);  // AND_Gate
  Multiplexer multiplexer_1 (.in0(RESET_PELA_PORTA_out), .in1(PINO_RESET), .out(CX_1));  // open: sel, en
  D_Flip_Flop d_ff_1 (.clk(CLOCK_INICIAL), .D(S___A), .Q(d_ff_1_q), .preset(CX_1));  // open: Qn, en, reset
  D_Flip_Flop d_ff_2 (.clk(d_ff_1_q), .D(S___B), .Q(d_ff_2_q), .preset(CX_1));  // open: Qn, en, reset
  D_Flip_Flop d_ff_3 (.clk(d_ff_2_q), .D(S___C), .Q(d_ff_3_q), .preset(CX_1));  // open: Qn, en, reset
  D_Flip_Flop d_ff_4 (.clk(d_ff_3_q), .D(S___D), .Q(d_ff_4_q), .preset(CX_1));  // open: Qn, en, reset
  not not_1 (S___A, d_ff_1_q);
  not not_2 (S___B, d_ff_2_q);
  not not_3 (S___C, d_ff_3_q);
  not not_4 (S___D, d_ff_4_q);
endmodule

module CLOCK_0_9 (
  input  CLCOCK,
  input  PINO_RESET,
  output S___A,
  output S___B,
  output S___C,
  output S___D,
  output CX_1
);

  wire d_ff_1_q, d_ff_2_q, d_ff_3_q, d_ff_4_q, RESET_PELA_PORTA_out;

  and RESET_PELA_PORTA (RESET_PELA_PORTA_out, ~S___A, S___B, ~S___C, S___D);  // AND_Gate
  Multiplexer multiplexer_1 (.in0(RESET_PELA_PORTA_out), .in1(PINO_RESET), .out(CX_1));  // open: sel, en
  D_Flip_Flop d_ff_1 (.clk(CLCOCK), .D(S___A), .Q(d_ff_1_q), .preset(CX_1));  // open: Qn, en, reset
  D_Flip_Flop d_ff_2 (.clk(d_ff_1_q), .D(S___B), .Q(d_ff_2_q), .preset(CX_1));  // open: Qn, en, reset
  D_Flip_Flop d_ff_3 (.clk(d_ff_2_q), .D(S___C), .Q(d_ff_3_q), .preset(CX_1));  // open: Qn, en, reset
  D_Flip_Flop d_ff_4 (.clk(d_ff_3_q), .D(S___D), .Q(d_ff_4_q), .preset(CX_1));  // open: Qn, en, reset
  not not_1 (S___A, d_ff_1_q);
  not not_2 (S___B, d_ff_2_q);
  not not_3 (S___C, d_ff_3_q);
  not not_4 (S___D, d_ff_4_q);
endmodule

module CLOCK_0_5 (
  input  PINO_RESET,
  output S___A,
  output S___B,
  output S___C,
  output S___D,
  output CX_1
);

  wire clock_1_out, d_ff_1_q, d_ff_2_q, d_ff_3_q, d_ff_4_q, RESET_PELA_PORTA_out;

  Clock clock_1 (.out(clock_1_out));
  and RESET_PELA_PORTA (RESET_PELA_PORTA_out, ~S___A, S___B, S___C, ~S___D);  // AND_Gate
  Multiplexer multiplexer_1 (.in0(RESET_PELA_PORTA_out), .in1(PINO_RESET), .out(CX_1));  // open: sel, en
  D_Flip_Flop d_ff_1 (.clk(clock_1_out), .D(S___A), .Q(d_ff_1_q), .preset(CX_1));  // open: Qn, en, reset
  D_Flip_Flop d_ff_2 (.clk(d_ff_1_q), .D(S___B), .Q(d_ff_2_q), .preset(CX_1));  // open: Qn, en, reset
  D_Flip_Flop d_ff_3 (.clk(d_ff_2_q), .D(S___C), .Q(d_ff_3_q), .preset(CX_1));  // open: Qn, en, reset
  D_Flip_Flop d_ff_4 (.clk(d_ff_3_q), .D(S___D), .Q(d_ff_4_q), .preset(CX_1));  // open: Qn, en, reset
  not not_1 (S___A, d_ff_1_q);
  not not_2 (S___B, d_ff_2_q);
  not not_3 (S___C, d_ff_3_q);
  not not_4 (S___D, d_ff_4_q);
endmodule

module relogio (
  input  g,
  input  f,
  input  a,
  input  b,
  input  in_5,
  input  e,
  input  d,
  input  c
);

  wire CK_I_p2, CK_I_p3, CK_I_p4, CK_I_p5, CK_I_p6, CLK_0_5_p2, CLK_0_5_p3, CLK_0_5_p4, CLK_0_5_p5,
       clock_1_out, decodificador_bcd_8421_p_7_1_a_2, decodificador_bcd_8421_p_7_1_b_2,
       decodificador_bcd_8421_p_7_1_c_2, decodificador_bcd_8421_p_7_1_d_2, decodificador_bcd_8421_p_7_1_e,
       decodificador_bcd_8421_p_7_1_f, decodificador_bcd_8421_p_7_1_g, decodificador_bcd_8421_p_7_2_a_2,
       decodificador_bcd_8421_p_7_2_b_2, decodificador_bcd_8421_p_7_2_c_2, decodificador_bcd_8421_p_7_2_d_2,
       decodificador_bcd_8421_p_7_2_e, decodificador_bcd_8421_p_7_2_f, decodificador_bcd_8421_p_7_2_g;

  CLOCK_INICIAL CLK_I ();  // open: CLOCK_INICIAL, PINO_RESET, S___A, S___B, S___C, S___D, CX_1
  Clock clock_1 (.out(clock_1_out));
  CLOCK_0_9 CLK_0_9 ();  // open: CLCOCK, PINO_RESET, S___A, S___B, S___C, S___D, CX_1
  // CLOCK_0_5 CLK_0_5: pin names not known; wires that end beside it: clock_1_out, CLK_0_5_p2, CLK_0_5_p3, CLK_0_5_p4, CLK_0_5_p5
  // CLOCK_INICIAL CK_I: pin names not known; wires that end beside it: in_5, CK_I_p2, CK_I_p3, CK_I_p4, CK_I_p5, CK_I_p6
  CLOCK_0_9 CK_0_9 (.CLCOCK(CK_I_p6));  // open: PINO_RESET, S___A, S___B, S___C, S___D, CX_1
  DECODIFICADOR_BCD_8421_P_7 decodificador_bcd_8421_p_7_1 (
    .D(CLK_0_5_p2), .C(CLK_0_5_p3), .B(CLK_0_5_p4), .A(CLK_0_5_p5), .a_2(decodificador_bcd_8421_p_7_1_a_2),
    .b_2(decodificador_bcd_8421_p_7_1_b_2), .c_2(decodificador_bcd_8421_p_7_1_c_2),
    .d_2(decodificador_bcd_8421_p_7_1_d_2), .e(decodificador_bcd_8421_p_7_1_e),
    .f(decodificador_bcd_8421_p_7_1_f), .g(decodificador_bcd_8421_p_7_1_g));
  DECODIFICADOR_BCD_8421_P_7 decodificador_bcd_8421_p_7_2 (
    .D(CK_I_p2), .C(CK_I_p3), .B(CK_I_p4), .A(CK_I_p5), .a_2(decodificador_bcd_8421_p_7_2_a_2),
    .b_2(decodificador_bcd_8421_p_7_2_b_2), .c_2(decodificador_bcd_8421_p_7_2_c_2),
    .d_2(decodificador_bcd_8421_p_7_2_d_2), .e(decodificador_bcd_8421_p_7_2_e),
    .f(decodificador_bcd_8421_p_7_2_f), .g(decodificador_bcd_8421_p_7_2_g));
  _7_Segment_Display u_7_segment_display_1 (
    .g(decodificador_bcd_8421_p_7_1_g), .f(decodificador_bcd_8421_p_7_1_f),
    .a(decodificador_bcd_8421_p_7_1_a_2), .b(decodificador_bcd_8421_p_7_1_b_2),
    .e(decodificador_bcd_8421_p_7_1_e), .d(decodificador_bcd_8421_p_7_1_d_2),
    .c(decodificador_bcd_8421_p_7_1_c_2));  // open: dp
  _7_Segment_Display u_7_segment_display_2 (
    .g(decodificador_bcd_8421_p_7_2_g), .f(decodificador_bcd_8421_p_7_2_f),
    .a(decodificador_bcd_8421_p_7_2_a_2), .b(decodificador_bcd_8421_p_7_2_b_2),
    .e(decodificador_bcd_8421_p_7_2_e), .d(decodificador_bcd_8421_p_7_2_d_2),
    .c(decodificador_bcd_8421_p_7_2_c_2));  // open: dp
  _7_Segment_Display u_7_segment_display_3 (.g(g), .f(f), .a(a), .b(b), .e(e), .d(d), .c(c));  // open: dp
endmodule

module DISPLAY (
  input  [3:0] in_1
);

  wire multiplexer_1_out, multiplexer_2_out, multiplexer_3_out, multiplexer_4_out, multiplexer_5_out,
       multiplexer_6_out, multiplexer_7_out;

  Multiplexer #(.select(4)) multiplexer_1 (
    .out(multiplexer_1_out), .sel(in_1));  // open: in0, in1, in2, in3, in4, in5, in6, in7, in8, in9, in10, in11, in12, in13, in14, in15, en
  Multiplexer #(.select(4)) multiplexer_2 (
    .out(multiplexer_2_out), .sel(in_1));  // open: in0, in1, in2, in3, in4, in5, in6, in7, in8, in9, in10, in11, in12, in13, in14, in15, en
  Multiplexer #(.select(4)) multiplexer_3 (
    .out(multiplexer_3_out), .sel(in_1));  // open: in0, in1, in2, in3, in4, in5, in6, in7, in8, in9, in10, in11, in12, in13, in14, in15, en
  Multiplexer #(.select(4)) multiplexer_4 (.out(multiplexer_4_out));  // open: in0, in1, in2, in3, in4, in5, in6, in7, in8, in9, in10, in11, in12, in13, in14, in15, sel, en
  Multiplexer #(.select(4)) multiplexer_5 (.out(multiplexer_5_out));  // open: in0, in1, in2, in3, in4, in5, in6, in7, in8, in9, in10, in11, in12, in13, in14, in15, sel, en
  Multiplexer #(.select(4)) multiplexer_6 (.out(multiplexer_6_out));  // open: in0, in1, in2, in3, in4, in5, in6, in7, in8, in9, in10, in11, in12, in13, in14, in15, sel, en
  Multiplexer #(.select(4)) multiplexer_7 (.out(multiplexer_7_out));  // open: in0, in1, in2, in3, in4, in5, in6, in7, in8, in9, in10, in11, in12, in13, in14, in15, sel, en
endmodule

module DECODIFICADOR_BCD_8421_P_7 (
  input  D,
  input  C,
  input  B,
  input  A,
  output a_2,
  output b_2,
  output c_2,
  output d_2,
  output e,
  output f,
  output g
);

  wire and_1_out, and_2_out, and_3_out, and_4_out, and_5_out, and_6_out, and_7_out, and_8_out, and_9_out,
       and_10_out, and_11_out, and_12_out, and_13_out, and_14_out, and_15_out, and_16_out, not_1_out,
       not_2_out, not_3_out, not_4_out, not_5_out, not_6_out, not_7_out, not_8_out, not_9_out, not_10_out,
       not_11_out, not_12_out, not_13_out, not_14_out, not_15_out, not_16_out, not_17_out, not_18_out,
       not_19_out, not_20_out, not_21_out;

  not not_1 (not_1_out, B);
  and and_1 (and_1_out, not_1_out, not_2_out);
  not not_2 (not_2_out, D);
  and and_2 (and_2_out, B, D);
  not not_3 (not_3_out, B);
  not not_4 (not_4_out, C);
  and and_3 (and_3_out, not_4_out, not_5_out);
  not not_5 (not_5_out, D);
  and and_4 (and_4_out, C, D);
  not not_6 (not_6_out, C);
  or or_1 (c_2, not_6_out, D, B);
  not not_7 (not_7_out, B);
  and and_5 (and_5_out, not_7_out, not_8_out);
  not not_8 (not_8_out, D);
  not not_9 (not_9_out, B);
  and and_6 (and_6_out, not_9_out, C);
  and and_7 (and_7_out, C, not_10_out);
  not not_10 (not_10_out, D);
  not not_11 (not_11_out, C);
  and and_8 (and_8_out, B, not_11_out, D);
  not not_12 (not_12_out, B);
  and and_9 (and_9_out, not_12_out, not_13_out);
  not not_13 (not_13_out, D);
  and and_10 (and_10_out, C, not_14_out);
  not not_14 (not_14_out, D);
  not not_15 (not_15_out, C);
  and and_11 (and_11_out, not_15_out, not_16_out);
  not not_16 (not_16_out, D);
  and and_12 (and_12_out, B, not_17_out);
  not not_17 (not_17_out, C);
  and and_13 (and_13_out, B, not_18_out);
  not not_18 (not_18_out, D);
  not not_19 (not_19_out, B);
  and and_14 (and_14_out, not_19_out, C);
  and and_15 (and_15_out, B, not_20_out);
  not not_20 (not_20_out, C);
  and and_16 (and_16_out, B, not_21_out);
  not not_21 (not_21_out, D);
  or or_2 (a_2, and_1_out, C, and_2_out, A);
  or or_3 (b_2, not_3_out, and_3_out, and_4_out);
  or or_4 (d_2, and_5_out, and_6_out, and_7_out, and_8_out, A);
  or or_5 (e, and_9_out, and_10_out);
  or or_6 (f, and_11_out, and_12_out, and_13_out, A);
  or or_7 (g, and_14_out, and_15_out, and_16_out, A);
endmodule

module ds (
  input  g,
  input  f,
  input  a,
  input  b,
  input  e,
  input  d,
  input  c
);

  _7_Segment_Display u_7_segment_display_1 (.g(g), .f(f), .a(a), .b(b), .e(e), .d(d), .c(c));  // open: dp
endmodule
